# Fritzing sketch smart bulb (saved by Fritzing 0.9.3b)

parts:
  MH-ET_LIVE_ESP32_DEVKIT1 = MH-ET LIVE ESP32 DEVKIT 38 pins
  M1 = ac light dimmer-4terminal
  JACK1 = 2.1mm Barrel Jack with Terminal Block
  LED1 = LED - 5mm [color="Red (633nm)" package="5 mm [THT]"]
  PIR1 = PIR sensor
  J1 = Piezo Speaker

nets:
  3V3: MH-ET_LIVE_ESP32_DEVKIT1.3V3, M1.VCC
  N1: MH-ET_LIVE_ESP32_DEVKIT1.IO14, PIR1.SIG
  5V: MH-ET_LIVE_ESP32_DEVKIT1.5V, PIR1.VDD
  N2: MH-ET_LIVE_ESP32_DEVKIT1.GND#64, PIR1.GND
  N3: MH-ET_LIVE_ESP32_DEVKIT1.GND#70, M1.GND, J1.pin1
  N4: MH-ET_LIVE_ESP32_DEVKIT1.IO19, M1.Z-C
  N5: MH-ET_LIVE_ESP32_DEVKIT1.IO18, M1.PWM
  N6: MH-ET_LIVE_ESP32_DEVKIT1.IO17, J1.pin2
  N7: M1.LOAD1, LED1.anode
  N8: M1.LOAD2, LED1.cathode
  N9: M1.AC-IN1, JACK1.NEG
  N10: M1.AC-IN2, JACK1.POS

notes:
  Smart Bulb
  220V

custom parts:
  MH-ET LIVE ESP32 DEVKIT 38 pins: http://mh.nodebb.com/topic/2/mh-et-live-esp32-devkit
  ac light dimmer-4terminal: ac light dimmer module 4terminal.
